# Fritzing sketch v2_fritzing (saved by Fritzing 0.9.4)
breadboards: 2

parts:
  Part1 = Solar Cell
  Part2 = Solar Cell
  Part3 = Solar Cell
  Part4 = Solar Cell
  R1 = Resistor [tolerance=±5% resistance=220 package="0603 [SMD]"]
  U1 = ESP32-38PinWide [part_number=ESP32-38PinWide]
  Part5 = Solar Cell
  Part6 = Solar Cell
  Part7 = Solar Cell
  Part8 = Solar Cell
  TP1 = TP4056 [chip_label=TP4056 package="DIP (Dual Inline) [THT]"]
  BAT1 = 18650 battery holder [package=battery-18650-kit]
  U2 = MPC1700 [package=sot23-3]
  C1 = Capacitor Polarized [package=cpol-radial-10uf-25v]

nets:
  N1: Part1.+, R1.Pin_1, U1.GPIO39
  N2: Part1.-, Part2.+
  GND: Part2.-, Part4.-, R1.Pin_0, U1.GND, TP1.pin6, BAT1.-, U2.GND, C1.-
  N3: Part3.+, U1.GPIO35
  N4: Part3.-, Part4.+
  N5: U1.3.3, U2.OUT, C1.+
  N6: Part5.+, TP1.pin2
  N7: Part5.-, Part6.+
  N8: Part6.-, Part7.+
  N9: Part7.-, Part8.+
  N10: Part8.-, TP1.pin1
  N11: TP1.pin3, BAT1.+, U2.IN

notes:
  1.5 V test panel
  1.5 V power panel
  TP4056
  MCP1700 3.3 V regulator
  Panasonic NCR18650B
  ESP32 NodeMCU

custom parts:
  ESP32-38PinWide: Generic 38-Pin ESP32 with wide format (only access to one side of pins on a breadboard) based on Stephen Lilley's HiLetgo ESP-WROOM-32 ESP32 ESP-32S Development Board.
  TP4056: A DIP stand-in part for whatever IC you want. With 6 pins on a 300mil dual inline package (DIP) footprint.
  18650 battery holder: 18650 Battery Holder
  MPC1700: Small package LDO
